# Fritzing sketch schematic (saved by Fritzing 0.9.1b)
breadboards: 1

parts:
  Part1 = Arduino Uno (Rev3)
  6V = DC Power [voltage=6]
  M1 = DC Motor
  M2 = DC Motor
  Part4 = L9110S Dual Motor Driver
  C1 = Electrolytic Capacitor [capacitance=47µF package="100 mil [THT, electrolytic]"]
  RF1 = nRF8001 Bluetooth LE Breakout

nets:
  N1: Part1.D9_PWM, RF1.RST
  N2: Part1.D10_PWM/SS, RF1.REQ
  N3: Part1.D11_PWM/MOSI, RF1.MOSI
  N4: Part1.D12/MISO, RF1.MISO
  N5: Part1.D13/SCK, RF1.SCK
  GND: Part1.GND, Part4.GND
  N6: Part1.D2, RF1.RDY
  N7: Part1.D4, Part4.B-IA
  N8: Part1.D5_PWM, Part4.B-IB
  N9: Part1.D6_PWM, Part4.A-IA
  N10: Part1.D7, Part4.A-IB
  5V: Part1.5V, RF1.VIN
  VIN: Part1.VIN, 6V.V+, Part4.VCC, C1.+
  N11: 6V.V-, C1.-, RF1.GND
  N12: M1.pin_1, Part4.B-OB
  N13: M1.pin_2, Part4.B-OA
  N14: M2.pin_1, Part4.A-OB
  N15: M2.pin_2, Part4.A-OA

custom parts:
  nRF8001 Bluetooth LE Breakout: nRF8001 Breakout Board
